# Fritzing sketch ambientsensorstation (saved by Fritzing 0.9.10b)
circuit board: 4.32cm x 4.02cm
breadboards: 1

parts:
  Switch = Pushbutton [package=THT]
  BME280 = GY-BMEP280 Barometric Pressure Sensor - Breakout
  NodeMCU = ESP8266 NodeMCU LoLin module
  GY-2561 = GY-2561 clone sensor from TSL2561
  CJMCU-811 = CJMCU-811
  LED1 = smd LED [color="Red (633nm)" package="0603 [SMD]"]  # not connected

nets:
  N1: Switch.leg0, NodeMCU.D3
  GND: Switch.leg1, BME280.GND, NodeMCU.GND, GY-2561.GND, CJMCU-811.GND, CJMCU-811.WAK
  N2: BME280.SDO, NodeMCU.D7
  N3: BME280.CSB, NodeMCU.D6
  N4: BME280.SDA, NodeMCU.D8
  N5: BME280.SCL, NodeMCU.D5
  VCC: BME280.VCC, NodeMCU.3V3, GY-2561.VCC, CJMCU-811.VCC
  N6: NodeMCU.D0, NodeMCU.RST
  N7: NodeMCU.D1, GY-2561.SCL, CJMCU-811.SCL
  N8: NodeMCU.D2, GY-2561.SDA, CJMCU-811.SDA

notes:
  ambient
  v1.0
  Lolin

custom parts:
  GY-BMEP280 Barometric Pressure Sensor - Breakout: The BME280 is a chip which was originally designed for the next generation of smartphones. It is made up of a very accurate pressure sensor and an associated temperature sensor which helps calibrate the pressure readings. And just for fun they threw in a pretty solid humidity sensor in there as well! So with an I2C connection you have access to enough weather data to make some pretty good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
  ESP8266 NodeMCU LoLin module: ESP8266 based NodeMCU
  CJMCU-811: The CCS811 is an ultra-low power digital gas sensor solution which integrates a metal oxide (MOX) gas sensor to detect a wide range of Volatile Organic Compounds (VOCs) for indoor air quality monitoring with a microcontroller unit (MCU), which includes an Analog-to-Digital converter (ADC), and an I²C interface.
